# Fritzing sketch Board Design (saved by Fritzing 0.9.4)
circuit board: 8.46667cm x 5.64444cm
breadboards: 1

parts:
  Part1 = Bluetooth HC-05 Macho
  Part2 = Arduino Uno (Rev3)
  LED1 = LED - 5mm [color="White (4500K)" package="5 mm [THT]"]
  LED2 = LED - 5mm [color="Blue (430nm)" package="5 mm [THT]"]

nets:
  N1: Part1.TXD, Part2.D9_PWM
  N2: Part1.RXD, Part2.D11_PWM/MOSI
  VCC: Part1.VCC, Part2.5V
  GND: Part1.GND, Part2.GND, LED1.cathode, LED2.cathode
  N3: Part2.D3_PWM, LED1.anode
  N4: Part2.D6_PWM, LED2.anode
